# Fritzing sketch Untitled Sketch (saved by Fritzing 0.9.3b)
breadboards: 1

parts:
  RHT1 = Humidity and Temperature Sensor RHT03
  Raspberry_Pi_1 = Raspberry Pi 3 [part_number=RPI-3-V1.2]
  R1 = Resistor [tolerance=±5% resistance=10k package="0603 [SMD]"]

nets:
  VCC: RHT1.Vcc, Raspberry_Pi_1.3v3, R1.Pin_0
  N1: RHT1.Data-signal, Raspberry_Pi_1.GPIO4, R1.Pin_1
  N2: RHT1.GND_2, Raspberry_Pi_1.GND
